// Logisim project CPU_Library.circ as structural Verilog
module AND (
  input  [5:0] A5_A0,
  input  [5:0] B5_B0,
  output [5:0] out_3
);

  and _0 (out_3[0], A5_A0[0], B5_B0[0]);
  and _1 (out_3[1], A5_A0[1], B5_B0[1]);
  and _2 (out_3[2], A5_A0[2], B5_B0[2]);
  and _3 (out_3[3], A5_A0[3], B5_B0[3]);
  and _4 (out_3[4], A5_A0[4], B5_B0[4]);
  and _5 (out_3[5], A5_A0[5], B5_B0[5]);

  // Other names for the same wires on the sheet: A0 = A5_A0[0]; A1 = A5_A0[1]; A2 = A5_A0[2]; A3 = A5_A0[3];
  //   A4 = A5_A0[4]; A5 = A5_A0[5]; B0 = B5_B0[0]; B1 = B5_B0[1]; B2 = B5_B0[2]; B3 = B5_B0[3]; B4 = B5_B0[4];
  //   B5 = B5_B0[5]; R0 = out_3[0]; R1 = out_3[1]; R2 = out_3[2]; R3 = out_3[3]; R4 = out_3[4]; R5 = out_3[5]
endmodule

module ROR (
  input  [5:0] A5_A0,
  input  [2:0] Shift_2_0,
  output [5:0] out_3
);

  Multiplexer #(.select(3), .enable("false")) multiplexer_1 (
    .in0(A5_A0[5]), .in1(A5_A0[0]), .in2(A5_A0[1]), .in3(A5_A0[2]), .in4(A5_A0[3]), .in5(A5_A0[4]),
    .in6(1'b0), .in7(1'b0), .out(out_3[5]), .sel(Shift_2_0));
  Multiplexer #(.select(3), .enable("false")) multiplexer_2 (
    .in0(A5_A0[4]), .in1(A5_A0[5]), .in2(A5_A0[0]), .in3(A5_A0[1]), .in4(A5_A0[2]), .in5(A5_A0[3]),
    .in6(1'b0), .in7(1'b0), .out(out_3[4]), .sel(Shift_2_0));
  Multiplexer #(.select(3), .enable("false")) multiplexer_3 (
    .in0(A5_A0[3]), .in1(A5_A0[4]), .in2(A5_A0[5]), .in3(A5_A0[0]), .in4(A5_A0[1]), .in5(A5_A0[2]),
    .in6(1'b0), .in7(1'b0), .out(out_3[3]), .sel(Shift_2_0));
  Multiplexer #(.select(3), .enable("false")) multiplexer_4 (
    .in0(A5_A0[2]), .in1(A5_A0[3]), .in2(A5_A0[4]), .in3(A5_A0[5]), .in4(A5_A0[0]), .in5(A5_A0[1]),
    .in6(1'b0), .in7(1'b0), .out(out_3[2]), .sel(Shift_2_0));
  Multiplexer #(.select(3), .enable("false")) multiplexer_5 (
    .in0(A5_A0[1]), .in1(A5_A0[2]), .in2(A5_A0[3]), .in3(A5_A0[4]), .in4(A5_A0[5]), .in5(A5_A0[0]),
    .in6(1'b0), .in7(1'b0), .out(out_3[1]), .sel(Shift_2_0));
  Multiplexer #(.select(3), .enable("false")) multiplexer_6 (
    .in0(A5_A0[0]), .in1(A5_A0[1]), .in2(A5_A0[2]), .in3(A5_A0[3]), .in4(A5_A0[4]), .in5(A5_A0[5]),
    .in6(1'b0), .in7(1'b0), .out(out_3[0]), .sel(Shift_2_0));

  // Other names for the same wires on the sheet: A0 = A5_A0[0]; A1 = A5_A0[1]; A2 = A5_A0[2]; A3 = A5_A0[3];
  //   A4 = A5_A0[4]; A5 = A5_A0[5]; R0 = out_3[0]; R1 = out_3[1]; R2 = out_3[2]; R3 = out_3[3]; R4 = out_3[4];
  //   R5 = out_3[5]
endmodule
